// Logisim project pipelined_v3.0_predictor.circ as structural Verilog: 23 circuits, main circuit main
module main (
);

  CPU cpu_1 ();  // open: out_1, out_2, out_3, out_4, out_5, out_6, out_7, out_8, out_9, out_10, out_11, out_12, out_13, out_14, out_15, out_16, out_17, out_18, out_19, out_20, out_21, out_22, out_23, out_24, out_25, out_26, out_27, out_28, out_29, out_30, out_31, out_32, out_33
endmodule

module CPU (
  output [19:0] out_1,
  output [31:0] out_2,
  output [31:0] out_3,
  output [31:0] out_4,
  output [31:0] out_5,
  output [31:0] out_6,
  output [31:0] out_7,
  output [31:0] out_8,
  output [31:0] out_9,
  output [31:0] out_10,
  output [31:0] out_11,
  output [31:0] out_12,
  output [31:0] out_13,
  output [31:0] out_14,
  output [31:0] out_15,
  output [31:0] out_16,
  output [31:0] out_17,
  output [31:0] out_18,
  output [31:0] out_19,
  output [31:0] out_20,
  output [31:0] out_21,
  output [31:0] out_22,
  output [31:0] out_23,
  output [31:0] out_24,
  output [31:0] out_25,
  output [31:0] out_26,
  output [31:0] out_27,
  output [31:0] out_28,
  output [31:0] out_29,
  output [31:0] out_30,
  output [31:0] out_31,
  output [31:0] out_32,
  output [31:0] out_33
);

  wire alu_1_condition_flag, ALUSrc, BEQ_BLT_BLTU, BNE_BGE_BGEU, CLK, ex_mem_1_memrd_2, ex_mem_1_memwr_2,
       ExtOp, JALR, Kill1, Kill2, M_to_R, Mem_to_Reg, MemRd, MemRd1, MemWr, RegWr1, RegWr2, RegWr3, SB_Type,
       SSET, Stall;
  wire [1:0] ForwardA, ForwardB, RdSrc;
  wire [4:0] ALUOp, instruction_spliter_1_rd_imml5, instruction_spliter_1_s2, Rd1, Rd2, Rd3, Rs, Rt;
  wire [5:0] OP;
  wire [10:0] Funct;
  wire [15:0] id_ex_1_immu_imml_2, Imm16, ImmU_ImmL, instruction_spliter_1_immediate16, multiplexer_2_out;
  wire [19:0] branch_predictor_1_next_pc_2, id_ex_1_pc_2, if_id_1_pc_2, next_pc_1_next_pc;
  wire [31:0] alu_1_result, ALUOut, data_memory_1_data_out, E_Imm16, ex_mem_1_data2_2, ex_mem_1_output_2,
       extender_1_out_3, id_ex_1_data1_2, id_ex_1_data2_2, if_id_1_instraction_2,
       instruction_memory_1_instruction, MEMOut, multiplexer_1_out, multiplexer_4_out, multiplexer_5_out,
       multiplexer_6_out, Output, PC_plus_1, register_file_1_read_data1, register_file_1_read_data2;

  Clock clock_1 (.out(CLK));
  PC pc_1 (.NextPC(branch_predictor_1_next_pc_2), .CLK(CLK), .PC(out_1), .Disable(Stall));
  Branch_Predictor branch_predictor_1 (
    .PC(out_1), .Branch_EX(Kill2), .Jump_ID(JALR), .Iinstruction(multiplexer_1_out),
    .Next_PC(next_pc_1_next_pc), .CLK(CLK), .Next_PC_2(branch_predictor_1_next_pc_2));
  Instruction_Memory instruction_memory_1 (.Address(out_1), .Instruction(instruction_memory_1_instruction));
  Multiplexer #(.width(32), .enable("false")) multiplexer_1 (
    .in0(instruction_memory_1_instruction), .in1({32{1'b0}}), .out(multiplexer_1_out), .sel(Kill1));
  IF_ID if_id_1 (
    .PC(out_1), .Instraction(multiplexer_1_out), .PC_2(if_id_1_pc_2), .Instraction_2(if_id_1_instraction_2),
    .CLK(CLK), .\disable (Stall));
  Instruction_Spliter instruction_spliter_1 (
    .in_1(if_id_1_instraction_2), .Op(OP), .S1(Rs), .Immediate16(instruction_spliter_1_immediate16),
    .F11_ImmU11(Funct), .Rd_ImmL5(instruction_spliter_1_rd_imml5), .ImmU_ImmL(ImmU_ImmL),
    .S2(instruction_spliter_1_s2));
  Multiplexer #(.width(16), .enable("false")) multiplexer_2 (
    .in0(instruction_spliter_1_immediate16), .in1(ImmU_ImmL), .out(multiplexer_2_out), .sel(SB_Type));
  Multiplexer #(.width(5), .enable("false")) multiplexer_3 (
    .in0(instruction_spliter_1_s2), .in1(instruction_spliter_1_rd_imml5), .out(Rt), .sel(SSET));
  // Probe on ForwardB
  Control_Unit control_unit_1 (
    .OP(OP), .ALUOp(ALUOp), .RdSrc(RdSrc), .RegWr(RegWr1), .ExtOp(ExtOp), .ALUSrc(ALUSrc), .MemRd(MemRd),
    .MemWr(MemWr), .Mem_to_reg(Mem_to_Reg), .SB_type(SB_Type), .SSET(SSET), .JALR(JALR),
    .BNE_BGE_BGEU(BNE_BGE_BGEU), .BEQ_BLT_BLTU(BEQ_BLT_BLTU), .Funct(Funct), .CLK(CLK), .Kill2(Kill2));
  // Probe on ForwardA
  Hazard_Detection_Unit hazard_detection_unit_1 (
    .Rs(Rs), .Rt(Rt), .Rd1(Rd1), .Rd2(Rd2), .Rd3(Rd3), .RegWr1(RegWr1), .RegWr2(RegWr2), .RegWr3(RegWr3),
    .MemRd(MemRd), .Stall(Stall), .ForwardA(ForwardA), .ForwardB(ForwardB), .MemRd1(MemRd1));
  Register_File register_file_1 (
    .R00(out_2), .R01(out_6), .R02(out_10), .R03(out_14), .R04(out_18), .R05(out_22), .R06(out_26),
    .R07(out_30), .R08(out_3), .R09(out_7), .R10(out_11), .R11(out_15), .R12(out_19),
    .Read_Data1(register_file_1_read_data1), .R13(out_23), .R14(out_27), .R15(out_31), .R16(out_4),
    .R17(out_8), .Rs(Rs), .Rt(Rt), .Rd(Rd3), .CLK(CLK), .Read_Data2(register_file_1_read_data2),
    .R18(out_12), .R19(out_16), .R20(out_20), .R21(out_24), .R22(out_28), .R23(out_32), .R24(out_5),
    .R25(out_9), .R26(out_13), .R27(out_17), .R28(out_21), .R29(out_25), .R30(out_29), .R31(out_33),
    .Write_Data(Output), .RegWrite(RegWr3));
  Extender extender_1 (.in_2(multiplexer_2_out), .out_3(extender_1_out_3), .in_1(ExtOp));
  ID_EX id_ex_1 (
    .PC(if_id_1_pc_2), .PC_2(id_ex_1_pc_2), .Imm16(multiplexer_2_out), .Imm16_2(Imm16), .CLK(CLK),
    .E_Imm16(extender_1_out_3), .E_Imm16_2(E_Imm16), .Data1(multiplexer_4_out), .Data1_2(id_ex_1_data1_2),
    .Data2(multiplexer_5_out), .Data2_2(id_ex_1_data2_2), .Rd(instruction_spliter_1_rd_imml5), .Rd_2(Rd1),
    .ImmU_ImmL(ImmU_ImmL), .ImmU_ImmL_2(id_ex_1_immu_imml_2), .MemRd(MemRd), .MemRd_2(MemRd1));
  Multiplexer #(.select(2), .width(32), .enable("false")) multiplexer_4 (
    .in0(register_file_1_read_data1), .in1(ALUOut), .in2(MEMOut), .in3(Output), .out(multiplexer_4_out),
    .sel(ForwardA));
  Multiplexer #(.select(2), .width(32), .enable("false")) multiplexer_5 (
    .in0(register_file_1_read_data2), .in1(ALUOut), .in2(MEMOut), .in3(Output), .out(multiplexer_5_out),
    .sel(ForwardB));
  Next_PC next_pc_1 (
    .Next_PC(next_pc_1_next_pc), .M_PC(id_ex_1_pc_2), .Immediate16(multiplexer_2_out),
    .condition_flag(alu_1_condition_flag), .JALR(JALR), .BEQ_BLT_BLTU(BEQ_BLT_BLTU),
    .BNE_BGE_BGEU(BNE_BGE_BGEU), .RS1(multiplexer_4_out), .PC_plus_1(PC_plus_1), .PC(out_1), .Kill2(Kill2),
    .ImmU_ImmL(id_ex_1_immu_imml_2), .Kill1(Kill1));
  Multiplexer #(.width(32), .enable("false")) multiplexer_6 (
    .in0(E_Imm16), .in1(id_ex_1_data2_2), .out(multiplexer_6_out), .sel(ALUSrc));
  ALU alu_1 (
    .Data1(id_ex_1_data1_2), .Data2(multiplexer_6_out), .Result(alu_1_result), .ALUOp(ALUOp),
    .condition_flag(alu_1_condition_flag));
  Multiplexer #(.select(2), .width(32), .enable("false")) multiplexer_7 (
    .in0(alu_1_result), .in1({id_ex_1_data2_2[15:0], Imm16}), .in2(PC_plus_1), .in3(E_Imm16), .out(ALUOut),
    .sel(RdSrc));
  EX_MEM ex_mem_1 (
    .MemRd(MemRd1), .MemRd_2(ex_mem_1_memrd_2), .MemWr(MemWr), .MemWr_2(ex_mem_1_memwr_2),
    .Mem_to_Reg(Mem_to_Reg), .Mem_to_Reg_2(M_to_R), .Output(ALUOut), .Output_2(ex_mem_1_output_2),
    .Data2(id_ex_1_data2_2), .Data2_2(ex_mem_1_data2_2), .Rd(Rd1), .Rd_2(Rd2), .CLK(CLK), .RegWr(RegWr1),
    .RegWr_2(RegWr2));
  Data_Memory data_memory_1 (
    .Address(ex_mem_1_output_2), .Data_out(data_memory_1_data_out), .Write(ex_mem_1_memwr_2),
    .Read(ex_mem_1_memrd_2), .CLK(CLK), .Data_in(ex_mem_1_data2_2));
  Multiplexer #(.width(32), .enable("false")) multiplexer_8 (
    .in0(ex_mem_1_output_2), .in1(data_memory_1_data_out), .out(MEMOut), .sel(M_to_R));
  MEM_WB mem_wb_1 (
    .RegWr(RegWr2), .RegWr_2(RegWr3), .Output(MEMOut), .Output_2(Output), .Rd(Rd2), .Rd_2(Rd3), .CLK(CLK));

  // Other names for the same wires on the sheet: PC[19:0] = out_1; R00[31:0] = out_2; R01[31:0] = out_6;
  //   R02[31:0] = out_10; R03[31:0] = out_14; R04[31:0] = out_18; R05[31:0] = out_22; R06[31:0] = out_26;
  //   R07[31:0] = out_30; R08[31:0] = out_3; R09[31:0] = out_7; R10[31:0] = out_11; R11[31:0] = out_15;
  //   R12[31:0] = out_19; R13[31:0] = out_23; R14[31:0] = out_27; R15[31:0] = out_31; R16[31:0] = out_4;
  //   R17[31:0] = out_8; R18[31:0] = out_12; R19[31:0] = out_16; R20[31:0] = out_20; R21[31:0] = out_24;
  //   R22[31:0] = out_28; R23[31:0] = out_32; R24[31:0] = out_5; R25[31:0] = out_9; R26[31:0] = out_13;
  //   R27[31:0] = out_17; R28[31:0] = out_21; R29[31:0] = out_25; R30[31:0] = out_29; R31[31:0] = out_33

  // Notes on the sheet:
  //   IF
  //   ID
  //   EX
  //   MEM
  //   WB
endmodule

module ALU (
  input  [4:0] ALUOp,
  input  [31:0] Data1,
  input  [31:0] Data2,
  output condition_flag,
  output [31:0] Result
);

  wire adder_1_carry_flag, adder_1_overflow_flag, not_1_out, xor_3_out, zero_detector_1_out_2;
  wire [31:0] and_1_out, Arithmetic, Logical, MUL, not_2_out, or_1_out, SEQ, Shift, SLT, SLTU, xor_1_out;

  Adder adder_1 (
    .Data1(Data1), .Data2(Data2), .Data_out(Arithmetic), .carry_flag(adder_1_carry_flag),
    .overflow_flag(adder_1_overflow_flag), .Add_Sub(ALUOp[0]));
  assign and_1_out = Data1 & Data2;  // AND_Gate and_1, 32 bits wide
  assign or_1_out = Data1 | Data2;  // OR_Gate or_1, 32 bits wide
  assign xor_1_out = Data1 ^ Data2;  // XOR_Gate xor_1, 32 bits wide
  Multiplier #(.width(31)) multiplier_1 (.a(Data1[30:0]), .b(Data2[30:0]), .out(MUL[30:0]));  // open: cin, cout
  xor xor_2 (MUL[31], Data1[30], Data2[30]);
  not not_1 (not_1_out, adder_1_carry_flag);
  Zero_Detector zero_detector_1 (.in_1(Arithmetic), .out_2(zero_detector_1_out_2));
  assign not_2_out = ~or_1_out;  // NOT_Gate not_2, 32 bits wide
  Shifter shifter_1 (.Shift_Amount(Data2[4:0]), .Data_in(Data1), .Shift_Rotate(ALUOp[1:0]), .Data_out(Shift));
  xor xor_3 (xor_3_out, adder_1_overflow_flag, Arithmetic[31]);
  assign SLT = {{31{1'b0}}, xor_3_out};  // Bit_Extender bit_extender_1
  assign SLTU = {{31{1'b0}}, not_1_out};  // Bit_Extender bit_extender_2
  assign SEQ = {{31{1'b0}}, zero_detector_1_out_2};  // Bit_Extender bit_extender_3
  Multiplexer #(.select(2), .width(32), .enable("false")) multiplexer_1 (
    .in0(and_1_out), .in1(or_1_out), .in2(not_2_out), .in3(xor_1_out), .out(Logical), .sel(ALUOp[1:0]));
  Multiplexer #(.select(3), .width(32), .enable("false")) multiplexer_2 (
    .in0(Shift), .in1(Arithmetic), .in2(SLT), .in3(SLTU), .in4(SEQ), .in5(Logical), .in6(MUL),
    .out({Result[31:1], condition_flag}), .sel(ALUOp[4:2]));  // open: in7

  assign Result[0] = condition_flag;

  // Other names for the same wires on the sheet: ALU_Selection[2:0] = ALUOp[4:2]
endmodule

module Register_File (
  input  [4:0] Rs,
  input  [4:0] Rt,
  input  [4:0] Rd,
  input  CLK,
  input  [31:0] Write_Data,
  input  RegWrite,
  output [31:0] R00,
  output [31:0] R01,
  output [31:0] R02,
  output [31:0] R03,
  output [31:0] R04,
  output [31:0] R05,
  output [31:0] R06,
  output [31:0] R07,
  output [31:0] R08,
  output [31:0] R09,
  output [31:0] R10,
  output [31:0] R11,
  output [31:0] R12,
  output [31:0] Read_Data1,
  output [31:0] R13,
  output [31:0] R14,
  output [31:0] R15,
  output [31:0] R16,
  output [31:0] R17,
  output [31:0] Read_Data2,
  output [31:0] R18,
  output [31:0] R19,
  output [31:0] R20,
  output [31:0] R21,
  output [31:0] R22,
  output [31:0] R23,
  output [31:0] R24,
  output [31:0] R25,
  output [31:0] R26,
  output [31:0] R27,
  output [31:0] R28,
  output [31:0] R29,
  output [31:0] R30,
  output [31:0] R31
);

  wire demultiplexer_1_out0, demultiplexer_1_out1, demultiplexer_1_out2, demultiplexer_1_out3,
       demultiplexer_1_out4, demultiplexer_1_out5, demultiplexer_1_out6, demultiplexer_1_out7,
       demultiplexer_1_out8, demultiplexer_1_out9, demultiplexer_1_out10, demultiplexer_1_out11,
       demultiplexer_1_out12, demultiplexer_1_out13, demultiplexer_1_out14, demultiplexer_1_out15,
       demultiplexer_1_out16, demultiplexer_1_out17, demultiplexer_1_out18, demultiplexer_1_out19,
       demultiplexer_1_out20, demultiplexer_1_out21, demultiplexer_1_out22, demultiplexer_1_out23,
       demultiplexer_1_out24, demultiplexer_1_out25, demultiplexer_1_out26, demultiplexer_1_out27,
       demultiplexer_1_out28, demultiplexer_1_out29, demultiplexer_1_out30, demultiplexer_1_out31;

  Demultiplexer #(.select(5), .enable("false")) demultiplexer_1 (
    .out0(demultiplexer_1_out0), .out1(demultiplexer_1_out1), .out2(demultiplexer_1_out2),
    .out3(demultiplexer_1_out3), .out4(demultiplexer_1_out4), .out5(demultiplexer_1_out5),
    .out6(demultiplexer_1_out6), .out7(demultiplexer_1_out7), .out8(demultiplexer_1_out8),
    .out9(demultiplexer_1_out9), .out10(demultiplexer_1_out10), .out11(demultiplexer_1_out11),
    .out12(demultiplexer_1_out12), .out13(demultiplexer_1_out13), .out14(demultiplexer_1_out14),
    .out15(demultiplexer_1_out15), .out16(demultiplexer_1_out16), .out17(demultiplexer_1_out17),
    .out18(demultiplexer_1_out18), .out19(demultiplexer_1_out19), .out20(demultiplexer_1_out20),
    .out21(demultiplexer_1_out21), .out22(demultiplexer_1_out22), .out23(demultiplexer_1_out23),
    .out24(demultiplexer_1_out24), .out25(demultiplexer_1_out25), .out26(demultiplexer_1_out26),
    .out27(demultiplexer_1_out27), .out28(demultiplexer_1_out28), .out29(demultiplexer_1_out29),
    .out30(demultiplexer_1_out30), .out31(demultiplexer_1_out31), .in(RegWrite), .sel(Rd));
  Register #(.width(32)) u_R00 (.D({32{1'b0}}), .en(demultiplexer_1_out0), .clk(CLK), .Q(R00));  // open: clr
  Register #(.width(32)) u_R01 (.D(Write_Data), .en(demultiplexer_1_out1), .clk(CLK), .Q(R01));  // open: clr
  Register #(.width(32)) u_R02 (.D(Write_Data), .en(demultiplexer_1_out2), .clk(CLK), .Q(R02));  // open: clr
  Register #(.width(32)) u_R03 (.D(Write_Data), .en(demultiplexer_1_out3), .clk(CLK), .Q(R03));  // open: clr
  Register #(.width(32)) u_R04 (.D(Write_Data), .en(demultiplexer_1_out4), .clk(CLK), .Q(R04));  // open: clr
  Register #(.width(32)) u_R05 (.D(Write_Data), .en(demultiplexer_1_out5), .clk(CLK), .Q(R05));  // open: clr
  Register #(.width(32)) u_R06 (.D(Write_Data), .en(demultiplexer_1_out6), .clk(CLK), .Q(R06));  // open: clr
  Register #(.width(32)) u_R07 (.D(Write_Data), .en(demultiplexer_1_out7), .clk(CLK), .Q(R07));  // open: clr
  Register #(.width(32)) u_R08 (.D(Write_Data), .en(demultiplexer_1_out8), .clk(CLK), .Q(R08));  // open: clr
  Register #(.width(32)) u_R09 (.D(Write_Data), .en(demultiplexer_1_out9), .clk(CLK), .Q(R09));  // open: clr
  Register #(.width(32)) u_R10 (.D(Write_Data), .en(demultiplexer_1_out10), .clk(CLK), .Q(R10));  // open: clr
  Register #(.width(32)) u_R11 (.D(Write_Data), .en(demultiplexer_1_out11), .clk(CLK), .Q(R11));  // open: clr
  Register #(.width(32)) u_R12 (.D(Write_Data), .en(demultiplexer_1_out12), .clk(CLK), .Q(R12));  // open: clr
  Register #(.width(32)) u_R13 (.D(Write_Data), .en(demultiplexer_1_out13), .clk(CLK), .Q(R13));  // open: clr
  Register #(.width(32)) u_R14 (.D(Write_Data), .en(demultiplexer_1_out14), .clk(CLK), .Q(R14));  // open: clr
  Register #(.width(32)) u_R15 (.D(Write_Data), .en(demultiplexer_1_out15), .clk(CLK), .Q(R15));  // open: clr
  Register #(.width(32)) u_R16 (.D(Write_Data), .en(demultiplexer_1_out16), .clk(CLK), .Q(R16));  // open: clr
  Register #(.width(32)) u_R17 (.D(Write_Data), .en(demultiplexer_1_out17), .clk(CLK), .Q(R17));  // open: clr
  Register #(.width(32)) u_R18 (.D(Write_Data), .en(demultiplexer_1_out18), .clk(CLK), .Q(R18));  // open: clr
  Register #(.width(32)) u_R19 (.D(Write_Data), .en(demultiplexer_1_out19), .clk(CLK), .Q(R19));  // open: clr
  Register #(.width(32)) u_R20 (.D(Write_Data), .en(demultiplexer_1_out20), .clk(CLK), .Q(R20));  // open: clr
  Register #(.width(32)) u_R21 (.D(Write_Data), .en(demultiplexer_1_out21), .clk(CLK), .Q(R21));  // open: clr
  Register #(.width(32)) u_R22 (.D(Write_Data), .en(demultiplexer_1_out22), .clk(CLK), .Q(R22));  // open: clr
  Register #(.width(32)) u_R23 (.D(Write_Data), .en(demultiplexer_1_out23), .clk(CLK), .Q(R23));  // open: clr
  Register #(.width(32)) u_R24 (.D(Write_Data), .en(demultiplexer_1_out24), .clk(CLK), .Q(R24));  // open: clr
  Register #(.width(32)) u_R25 (.D(Write_Data), .en(demultiplexer_1_out25), .clk(CLK), .Q(R25));  // open: clr
  Register #(.width(32)) u_R26 (.D(Write_Data), .en(demultiplexer_1_out26), .clk(CLK), .Q(R26));  // open: clr
  Register #(.width(32)) u_R27 (.D(Write_Data), .en(demultiplexer_1_out27), .clk(CLK), .Q(R27));  // open: clr
  Register #(.width(32)) u_R28 (.D(Write_Data), .en(demultiplexer_1_out28), .clk(CLK), .Q(R28));  // open: clr
  Register #(.width(32)) u_R29 (.D(Write_Data), .en(demultiplexer_1_out29), .clk(CLK), .Q(R29));  // open: clr
  Register #(.width(32)) u_R30 (.D(Write_Data), .en(demultiplexer_1_out30), .clk(CLK), .Q(R30));  // open: clr
  Register #(.width(32)) u_R31 (.D(Write_Data), .en(demultiplexer_1_out31), .clk(CLK), .Q(R31));  // open: clr
  Multiplexer #(.select(5), .width(32), .enable("false")) multiplexer_1 (
    .in0(R00), .in1(R01), .in2(R02), .in3(R03), .in4(R04), .in5(R05), .in6(R06), .in7(R07), .in8(R08),
    .in9(R09), .in10(R10), .in11(R11), .in12(R12), .in13(R13), .in14(R14), .in15(R15), .in16(R16),
    .in17(R17), .in18(R18), .in19(R19), .in20(R20), .in21(R21), .in22(R22), .in23(R23), .in24(R24),
    .in25(R25), .in26(R26), .in27(R27), .in28(R28), .in29(R29), .in30(R30), .in31(R31), .out(Read_Data1),
    .sel(Rs));
  Multiplexer #(.select(5), .width(32), .enable("false")) multiplexer_2 (
    .in0(R00), .in1(R01), .in2(R02), .in3(R03), .in4(R04), .in5(R05), .in6(R06), .in7(R07), .in8(R08),
    .in9(R09), .in10(R10), .in11(R11), .in12(R12), .in13(R13), .in14(R14), .in15(R15), .in16(R16),
    .in17(R17), .in18(R18), .in19(R19), .in20(R20), .in21(R21), .in22(R22), .in23(R23), .in24(R24),
    .in25(R25), .in26(R26), .in27(R27), .in28(R28), .in29(R29), .in30(R30), .in31(R31), .out(Read_Data2),
    .sel(Rt));
endmodule

module PC (
  input  [19:0] NextPC,
  input  Disable,
  input  CLK,
  output [19:0] PC
);

  wire not_1_out;

  Register #(.width(20)) u_PC (.D(NextPC), .en(not_1_out), .clk(CLK), .Q(PC));  // open: clr
  not not_1 (not_1_out, Disable);
endmodule

module Instruction_Memory (
  input  [19:0] Address,
  output [31:0] Instruction
);

  ROM #(.addrWidth(20), .dataWidth(32)) rom_1 (.addr(Address), .data(Instruction));

  // Notes on the sheet:
  //   contents of rom_1 (hex, n*v repeats v):
  //   1004d 10011 10051 a008d 20091 128900cd 45ac00ce 230711 500010d 7342010e 240751 384004d 1234020d
  //   5678020e 140945 12508c0 834100 50 10090 200d0 a42100 841100 c31180 30d2 820880 ffe00712 40011
  //   1a31280 245380 4453c0 57684 2501cf 4545024d 4545028d 95095 ffff0dcb 12 1431140 50 50890 608d0
  //   1631100 40011 380f
endmodule

module Data_Memory (
  input  Read,
  input  Write,
  input  [31:0] Address,
  input  CLK,
  input  [31:0] Data_in,
  output [31:0] Data_out
);

  RAM #(.addrWidth(20), .dataWidth(32), .trigger("falling"), .databus("bibus")) ram_1 (
    .addr(Address[19:0]), .we(Write), .oe(Read), .clk(CLK), .din(Data_in), .dout(Data_out));
endmodule

module Instruction_Spliter (
  input  [31:0] in_1,
  output [15:0] Immediate16,
  output [10:0] F11_ImmU11,
  output [4:0] S2,
  output [4:0] Rd_ImmL5,
  output [5:0] Op,
  output [4:0] S1,
  output [15:0] ImmU_ImmL
);


  assign F11_ImmU11 = in_1[31:21];
  assign Immediate16 = in_1[31:16];
  assign ImmU_ImmL = {in_1[31:21], in_1[10:6]};
  assign Op = in_1[5:0];
  assign Rd_ImmL5 = in_1[10:6];
  assign S1 = in_1[15:11];
  assign S2 = in_1[20:16];
endmodule

module Next_PC (
  input  [19:0] PC,
  input  JALR,
  input  [31:0] RS1,
  input  [15:0] Immediate16,
  input  BNE_BGE_BGEU,
  input  BEQ_BLT_BLTU,
  input  [15:0] ImmU_ImmL,
  input  condition_flag,
  input  [19:0] M_PC,
  output Kill1,
  output Kill2,
  output [19:0] Next_PC,
  output [31:0] PC_plus_1
);

  wire and_2_out, and_3_out;
  wire [1:1] and_1_out;
  wire [19:0] adder_1_out, adder_2_out, adder_3_out, adder_4_out, bit_extender_1_out, bit_extender_2_out;

  assign bit_extender_1_out = {{4{Immediate16[15]}}, Immediate16};  // Bit_Extender bit_extender_1
  assign bit_extender_2_out = {{4{ImmU_ImmL[15]}}, ImmU_ImmL};  // Bit_Extender bit_extender_2
  Adder_part #(.width(20)) adder_1 (.a(20'h1), .b(M_PC), .out(adder_1_out));  // open: cin, cout
  Adder_part #(.width(20)) adder_2 (.a(20'h1), .b(PC), .out(adder_2_out));  // open: cin, cout
  Multiplexer #(.select(2), .width(20), .enable("false")) multiplexer_1 (
    .in0(adder_2_out), .in1(adder_4_out), .in2(adder_3_out), .out(Next_PC), .sel({and_1_out[1], Kill2}));  // open: in3
  Adder_part #(.width(20)) adder_3 (.a(RS1[19:0]), .b(bit_extender_1_out), .out(adder_3_out));  // open: cin, cout
  Adder_part #(.width(20)) adder_4 (.a(bit_extender_2_out), .b(M_PC), .out(adder_4_out));  // open: cin, cout
  assign PC_plus_1 = {{12{1'b0}}, adder_1_out};  // Bit_Extender bit_extender_3
  or or_1 (Kill1, and_1_out[1], Kill2);
  and and_1 (and_1_out[1], JALR, ~Kill2);  // AND_Gate
  or or_2 (Kill2, and_2_out, and_3_out);
  and and_2 (and_2_out, BEQ_BLT_BLTU, condition_flag);
  and and_3 (and_3_out, BNE_BGE_BGEU, ~condition_flag);  // AND_Gate
endmodule

module Control_Unit (
  input  [5:0] OP,
  input  [10:0] Funct,
  input  Kill2,
  input  CLK,
  output [4:0] ALUOp,
  output [1:0] RdSrc,
  output RegWr,
  output ExtOp,
  output ALUSrc,
  output MemRd,
  output MemWr,
  output Mem_to_reg,
  output SB_type,
  output SSET,
  output JALR,
  output BNE_BGE_BGEU,
  output BEQ_BLT_BLTU
);

  wire [17:0] multiplexer_1_out, rom_1_data;

  ROM #(.addrWidth(9), .dataWidth(18)) rom_1 (.addr({OP[4:0], Funct[3:0]}), .data(rom_1_data));
  Multiplexer #(.width(18), .enable("false")) multiplexer_1 (
    .in0(rom_1_data), .in1({18{1'b0}}),
    .out({multiplexer_1_out[17:10], ExtOp, multiplexer_1_out[8], MemRd, multiplexer_1_out[6:5], SB_type, SSET, JALR, multiplexer_1_out[1:0]}),
    .sel(Kill2));
  Control_Signals control_signals_1 (
    .ALUOp(multiplexer_1_out[17:13]), .RdSrc(multiplexer_1_out[12:11]), .RegWr(multiplexer_1_out[10]),
    .ALUSrc(multiplexer_1_out[8]), .MemWr(multiplexer_1_out[6]), .Mem_to_Reg(multiplexer_1_out[5]),
    .BNE_BGE_BGEU(multiplexer_1_out[1]), .BEQ_BLT_BLTU(multiplexer_1_out[0]), .PC(ALUOp), .RdSrc_2(RdSrc),
    .RegWr_2(RegWr), .ALUSrc_2(ALUSrc), .MemWr_2(MemWr), .Mem_to_Reg_2(Mem_to_reg),
    .BNE_BGE_BGEU_2(BNE_BGE_BGEU), .BEQ_BLT_BLTU_2(BEQ_BLT_BLTU), .CLK(CLK));

  // Notes on the sheet:
  //   contents of rom_1 (hex, n*v repeats v):
  //   500 2500 4500 6500 8500 a500 12500 1a500 22500 2e500 2a500 28500 2c500 30500 0 0 16*400 16*2400
  //   16*4400 16*6400 16*8600 16*12600 16*1a400 16*22600 16*2e400 16*2a400 16*28400 16*2c400 16*1e00
  //   16*c08 16*1404 16*86a0 16*8250 16*22111 16*22112 16*12111 16*12112 16*1a111 16*1a112
endmodule

module Adder (
  input  Add_Sub,
  input  [31:0] Data1,
  input  [31:0] Data2,
  output [31:0] Data_out,
  output carry_flag,
  output overflow_flag
);

  wire xor_2_out, xor_3_out;
  wire [31:0] bit_extender_1_out, xor_1_out;

  assign bit_extender_1_out = {{31{Add_Sub}}, Add_Sub};  // Bit_Extender bit_extender_1
  assign xor_1_out = Data2 ^ bit_extender_1_out;  // XOR_Gate xor_1, 32 bits wide
  Adder_part #(.width(32)) adder_1 (.a(Data1), .b(xor_1_out), .out(Data_out), .cin(Add_Sub), .cout(carry_flag));
  xor xor_2 (xor_2_out, Data_out[31], Data1[31]);
  xor xor_3 (xor_3_out, Data_out[31], xor_1_out[31]);
  and and_1 (overflow_flag, xor_2_out, xor_3_out);
endmodule

module Shifter (
  input  [4:0] Shift_Amount,
  input  [31:0] Data_in,
  input  [1:0] Shift_Rotate,
  output [31:0] Data_out
);

  wire [31:0] shifter_1_out, shifter_2_out, shifter_3_out, shifter_4_out;

  Shifter_part #(.width(32)) shifter_1 (.in(Data_in), .\dist (Shift_Amount), .out(shifter_1_out));
  Shifter_part #(.width(32), .shift("lr")) shifter_2 (.in(Data_in), .\dist (Shift_Amount), .out(shifter_2_out));
  Shifter_part #(.width(32), .shift("ar")) shifter_3 (.in(Data_in), .\dist (Shift_Amount), .out(shifter_3_out));
  Shifter_part #(.width(32), .shift("rr")) shifter_4 (.in(Data_in), .\dist (Shift_Amount), .out(shifter_4_out));
  Multiplexer #(.select(2), .width(32), .enable("false")) multiplexer_1 (
    .in0(shifter_1_out), .in1(shifter_2_out), .in2(shifter_3_out), .in3(shifter_4_out), .out(Data_out),
    .sel(Shift_Rotate));

  // Notes on the sheet:
  //   Operation
endmodule

module Extender (
  input  in_1,
  input  [15:0] in_2,
  output [31:0] out_3
);

  wire [31:0] bit_extender_1_out, bit_extender_2_out;

  assign bit_extender_1_out = {{16{1'b0}}, in_2};  // Bit_Extender bit_extender_1
  assign bit_extender_2_out = {{16{in_2[15]}}, in_2};  // Bit_Extender bit_extender_2
  Multiplexer #(.width(32), .enable("false")) multiplexer_1 (
    .in0(bit_extender_1_out), .in1(bit_extender_2_out), .out(out_3), .sel(in_1));
endmodule

module Zero_Detector (
  input  [31:0] in_1,
  output out_2
);

  nor nor_1 (out_2, in_1[31], in_1[30], in_1[29], in_1[28], in_1[27], in_1[26], in_1[25], in_1[24], in_1[23], in_1[22], in_1[21], in_1[20], in_1[19], in_1[18], in_1[17], in_1[16], in_1[15], in_1[14], in_1[13], in_1[12], in_1[11], in_1[10], in_1[9], in_1[8], in_1[7], in_1[6], in_1[5], in_1[4], in_1[3], in_1[2], in_1[1], in_1[0]);
endmodule

module IF_ID (
  input  [19:0] PC,
  input  [31:0] Instraction,
  input  \disable ,
  input  CLK,
  output [19:0] PC_2,
  output [31:0] Instraction_2
);

  wire not_1_out;

  not not_1 (not_1_out, \disable );
  Register #(.width(20)) register_1 (.D(PC), .en(not_1_out), .clk(CLK), .Q(PC_2));  // open: clr
  Register #(.width(32)) register_2 (.D(Instraction), .en(not_1_out), .clk(CLK), .Q(Instraction_2));  // open: clr
endmodule

module ID_EX (
  input  [19:0] PC,
  input  [15:0] ImmU_ImmL,
  input  [15:0] Imm16,
  input  MemRd,
  input  [31:0] E_Imm16,
  input  [31:0] Data1,
  input  [31:0] Data2,
  input  [4:0] Rd,
  input  CLK,
  output [19:0] PC_2,
  output [15:0] ImmU_ImmL_2,
  output [15:0] Imm16_2,
  output MemRd_2,
  output [31:0] E_Imm16_2,
  output [31:0] Data1_2,
  output [31:0] Data2_2,
  output [4:0] Rd_2
);

  Register #(.width(20)) register_1 (.D(PC), .en(1'b1), .clk(CLK), .Q(PC_2));  // open: clr
  Register #(.width(16)) register_2 (.D(ImmU_ImmL), .en(1'b1), .clk(CLK), .Q(ImmU_ImmL_2));  // open: clr
  Register #(.width(16)) register_3 (.D(Imm16), .en(1'b1), .clk(CLK), .Q(Imm16_2));  // open: clr
  Register #(.width(1)) register_4 (.D(MemRd), .en(1'b1), .clk(CLK), .Q(MemRd_2));  // open: clr
  Register #(.width(32)) register_5 (.D(E_Imm16), .en(1'b1), .clk(CLK), .Q(E_Imm16_2));  // open: clr
  Register #(.width(32)) register_6 (.D(Data1), .en(1'b1), .clk(CLK), .Q(Data1_2));  // open: clr
  Register #(.width(32)) register_7 (.D(Data2), .en(1'b1), .clk(CLK), .Q(Data2_2));  // open: clr
  Register #(.width(5)) register_8 (.D(Rd), .en(1'b1), .clk(CLK), .Q(Rd_2));  // open: clr
endmodule

module EX_MEM (
  input  RegWr,
  input  MemRd,
  input  MemWr,
  input  Mem_to_Reg,
  input  [31:0] Output,
  input  [31:0] Data2,
  input  [4:0] Rd,
  input  CLK,
  output RegWr_2,
  output MemRd_2,
  output MemWr_2,
  output Mem_to_Reg_2,
  output [31:0] Output_2,
  output [31:0] Data2_2,
  output [4:0] Rd_2
);

  Register #(.width(1)) register_1 (.D(RegWr), .en(1'b1), .clk(CLK), .Q(RegWr_2));  // open: clr
  Register #(.width(1)) register_2 (.D(MemRd), .en(1'b1), .clk(CLK), .Q(MemRd_2));  // open: clr
  Register #(.width(1)) register_3 (.D(MemWr), .en(1'b1), .clk(CLK), .Q(MemWr_2));  // open: clr
  Register #(.width(1)) register_4 (.D(Mem_to_Reg), .en(1'b1), .clk(CLK), .Q(Mem_to_Reg_2));  // open: clr
  Register #(.width(32)) register_5 (.D(Output), .en(1'b1), .clk(CLK), .Q(Output_2));  // open: clr
  Register #(.width(32)) register_6 (.D(Data2), .en(1'b1), .clk(CLK), .Q(Data2_2));  // open: clr
  Register #(.width(5)) register_7 (.D(Rd), .en(1'b1), .clk(CLK), .Q(Rd_2));  // open: clr
endmodule

module MEM_WB (
  input  RegWr,
  input  [31:0] Output,
  input  [4:0] Rd,
  input  CLK,
  output RegWr_2,
  output [31:0] Output_2,
  output [4:0] Rd_2
);

  Register #(.width(1)) register_1 (.D(RegWr), .en(1'b1), .clk(CLK), .Q(RegWr_2));  // open: clr
  Register #(.width(32)) register_2 (.D(Output), .en(1'b1), .clk(CLK), .Q(Output_2));  // open: clr
  Register #(.width(5)) register_3 (.D(Rd), .en(1'b1), .clk(CLK), .Q(Rd_2));  // open: clr
endmodule

module Control_Signals (
  input  [4:0] ALUOp,
  input  [1:0] RdSrc,
  input  RegWr,
  input  ALUSrc,
  input  MemWr,
  input  Mem_to_Reg,
  input  BNE_BGE_BGEU,
  input  BEQ_BLT_BLTU,
  input  CLK,
  output [4:0] PC,
  output [1:0] RdSrc_2,
  output RegWr_2,
  output ALUSrc_2,
  output MemWr_2,
  output Mem_to_Reg_2,
  output BNE_BGE_BGEU_2,
  output BEQ_BLT_BLTU_2
);

  Register #(.width(5)) register_1 (.D(ALUOp), .en(1'b1), .clk(CLK), .Q(PC));  // open: clr
  Register #(.width(2)) register_2 (.D(RdSrc), .en(1'b1), .clk(CLK), .Q(RdSrc_2));  // open: clr
  Register #(.width(1)) register_3 (.D(RegWr), .en(1'b1), .clk(CLK), .Q(RegWr_2));  // open: clr
  Register #(.width(1)) register_4 (.D(ALUSrc), .en(1'b1), .clk(CLK), .Q(ALUSrc_2));  // open: clr
  Register #(.width(1)) register_5 (.D(MemWr), .en(1'b1), .clk(CLK), .Q(MemWr_2));  // open: clr
  Register #(.width(1)) register_6 (.D(Mem_to_Reg), .en(1'b1), .clk(CLK), .Q(Mem_to_Reg_2));  // open: clr
  Register #(.width(1)) register_7 (.D(BNE_BGE_BGEU), .en(1'b1), .clk(CLK), .Q(BNE_BGE_BGEU_2));  // open: clr
  Register #(.width(1)) register_8 (.D(BEQ_BLT_BLTU), .en(1'b1), .clk(CLK), .Q(BEQ_BLT_BLTU_2));  // open: clr
endmodule

module Hazard_Detection_Unit (
  input  [4:0] Rs,
  input  [4:0] Rt,
  input  [4:0] Rd1,
  input  [4:0] Rd2,
  input  [4:0] Rd3,
  input  RegWr1,
  input  RegWr2,
  input  RegWr3,
  input  MemRd,
  input  MemRd1,
  output [1:0] ForwardA,
  output [1:0] ForwardB,
  output Stall
);

  wire and_1_out, and_2_out, and_3_out, and_4_out, ForwardA1, ForwardA2, ForwardA3, ForwardB1, ForwardB2,
       ForwardB3, or_1_out, or_2_out, or_5_out;

  Forwarding forwarding_1 (.Rs_Rt(Rs), .Rd(Rd1), .RegWr(RegWr1), .Forward(ForwardA1));
  Forwarding forwarding_2 (.Rs_Rt(Rs), .Rd(Rd2), .RegWr(RegWr2), .Forward(ForwardA2));
  Forwarding forwarding_3 (.Rs_Rt(Rs), .Rd(Rd3), .RegWr(RegWr3), .Forward(ForwardA3));
  Forwarding forwarding_4 (.Rs_Rt(Rt), .Rd(Rd1), .RegWr(RegWr1), .Forward(ForwardB1));
  Forwarding forwarding_5 (.Rs_Rt(Rt), .Rd(Rd2), .RegWr(RegWr2), .Forward(ForwardB2));
  Forwarding forwarding_6 (.Rs_Rt(Rt), .Rd(Rd3), .RegWr(RegWr3), .Forward(ForwardB3));
  and and_1 (and_1_out, ~ForwardA2, ForwardA3);  // AND_Gate
  or or_1 (or_1_out, ForwardA2, ForwardA3);
  and and_2 (and_2_out, ~ForwardB2, ForwardB3);  // AND_Gate
  or or_2 (or_2_out, ForwardB2, ForwardB3);
  and and_3 (and_3_out, ~ForwardA[1], ForwardA[0]);  // AND_Gate
  and and_4 (and_4_out, ForwardB[0], ~ForwardB[1], ~MemRd);  // AND_Gate
  or or_3 (ForwardA[0], ForwardA1, and_1_out);
  and and_5 (ForwardA[1], ~ForwardA1, or_1_out);  // AND_Gate
  or or_4 (ForwardB[0], ForwardB1, and_2_out);
  and and_6 (ForwardB[1], ~ForwardB1, or_2_out);  // AND_Gate
  or or_5 (or_5_out, and_3_out, and_4_out);
  and and_7 (Stall, MemRd1, or_5_out);
endmodule

module Forwarding (
  input  [4:0] Rs_Rt,
  input  [4:0] Rd,
  input  RegWr,
  output Forward
);

  wire comparator_1_eq, or_1_out;

  or or_1 (or_1_out, Rs_Rt[0], Rs_Rt[1], Rs_Rt[2], Rs_Rt[3], Rs_Rt[4]);
  Comparator #(.width(5)) comparator_1 (.a(Rs_Rt), .b(Rd), .eq(comparator_1_eq));  // open: gt, lt
  and and_1 (Forward, or_1_out, comparator_1_eq, RegWr);
endmodule

module Branch_Predictor (
  input  [19:0] PC,
  input  CLK,
  input  [19:0] Next_PC,
  input  Branch_EX,
  input  Jump_ID,
  input  [31:0] Iinstruction,
  output [19:0] Next_PC_2
);

  wire Address_Found, and_5_out, and_6_out, and_9_out, and_10_out, and_11_out, Branch, Entry_Found,
       Entry_Found_EX, Entry_Found_EX_2, Entry_Found_ID, Jamp, Jump_ID_t, Jump_or_Branch, or_4_out, or_5_out,
       Predict_Taken, Predict_Taken_EX, Predict_Taken_EX_2, Predict_Taken_ID, Unkown_Entry, Unkown_Entry_EX,
       Unkown_Entry_EX_2, Unkown_Entry_ID, Unkown_Jump_or_Branch, xor_1_out;
  wire [0:0] ram_3_dout;
  wire [1:0] multiplexer_5_out, Target_Address_Src, two_bit_couter_1_output;
  wire [3:0] multiplexer_1_out, multiplexer_2_out, multiplexer_3_out, multiplexer_4_out, Predict_Address_EX,
       Predict_Address_EX_2, Predict_Address_ID;
  wire [19:0] ram_1_dout, Target_Address_Output;

  and and_1 (Unkown_Entry, ~Address_Found, Jump_or_Branch);  // AND_Gate
  and and_2 (Entry_Found, Address_Found, Jump_or_Branch);
  and and_3 (Jump_ID_t, ~Branch_EX, Jump_ID);  // AND_Gate
  Multiplexer #(.width(4), .enable("false")) multiplexer_1 (
    .in0(PC[3:0]), .in1(Predict_Address_ID), .out(multiplexer_1_out), .sel(Unkown_Entry));
  RAM #(.addrWidth(4), .dataWidth(20), .databus("bibus")) ram_1 (
    .addr(multiplexer_1_out), .we(Unkown_Entry), .oe(1'b1), .clk(CLK), .din(PC), .dout(ram_1_dout));
  and and_4 (Jamp, ~Iinstruction[4], Iinstruction[3], Iinstruction[2], Iinstruction[1], Iinstruction[0]);  // AND_Gate
  and and_5 (and_5_out, Iinstruction[4], ~Iinstruction[3], Iinstruction[2]);  // AND_Gate
  or or_1 (Branch, and_5_out, and_6_out);
  and and_6 (and_6_out, Iinstruction[4], ~Iinstruction[3], Iinstruction[1]);  // AND_Gate
  or or_2 (Jump_or_Branch, Jamp, Branch);
  Comparator #(.width(20)) comparator_1 (.a(ram_1_dout), .b(PC), .eq(Address_Found));  // open: gt, lt
  Multiplexer #(.select(2), .width(4), .enable("false")) multiplexer_2 (
    .in0(PC[3:0]), .in1(Predict_Address_EX), .in2(Predict_Address_EX_2), .out(multiplexer_2_out),
    .sel(Target_Address_Src));  // open: in3
  RAM #(.addrWidth(4), .dataWidth(20), .databus("bibus")) ram_2 (
    .addr(multiplexer_2_out), .we(Unkown_Jump_or_Branch), .oe(1'b1), .clk(CLK), .din(Next_PC),
    .dout(Target_Address_Output));
  and and_7 (Target_Address_Src[0], Jump_ID_t, Unkown_Entry_ID);
  and and_8 (Target_Address_Src[1], Unkown_Entry_EX, Branch_EX);
  or or_3 (Unkown_Jump_or_Branch, Target_Address_Src[0], Target_Address_Src[1]);
  Multiplexer #(.width(4), .enable("false")) multiplexer_3 (
    .in0(PC[3:0]), .in1(Predict_Address_ID), .out(multiplexer_3_out), .sel(Unkown_Entry));
  xor xor_1 (xor_1_out, Branch_EX, Predict_Taken_EX);
  Multiplexer #(.select(2), .width(4), .enable("false")) multiplexer_4 (
    .in0(multiplexer_3_out), .in1(Predict_Address_EX), .in2(Predict_Address_EX_2), .out(multiplexer_4_out),
    .sel({Branch_EX, Jump_ID_t}));  // open: in3
  RAM #(.addrWidth(4), .dataWidth(2), .databus("bibus")) ram_3 (
    .addr(multiplexer_4_out), .we(or_4_out), .oe(1'b1), .clk(CLK), .din(multiplexer_5_out),
    .dout({Predict_Taken, ram_3_dout[0]}));
  or or_4 (or_4_out, xor_1_out, Jump_ID_t, Unkown_Entry);
  Multiplexer #(.width(2), .enable("false")) multiplexer_5 (
    .in0(two_bit_couter_1_output), .in1(2'b10), .out(multiplexer_5_out), .sel(Unkown_Entry));
  Multiplexer #(.width(20), .enable("false")) multiplexer_6 (
    .in0(Next_PC), .in1(Target_Address_Output), .out(Next_PC_2), .sel(and_9_out));
  and and_9 (and_9_out, Predict_Taken, Entry_Found, ~Unkown_Jump_or_Branch);  // AND_Gate
  two_bit_couter two_bit_couter_1 (
    .Input({Predict_Taken, ram_3_dout[0]}), .Count_Up_Down(or_5_out), .Output(two_bit_couter_1_output));
  and and_10 (and_10_out, Branch_EX, ~Predict_Taken_EX);  // AND_Gate
  or or_5 (or_5_out, and_10_out, Jump_ID_t);
  and and_11 (and_11_out, ~Branch_EX, Predict_Taken_EX);  // AND_Gate
  Register #(.width(1)) register_1 (.D(Predict_Taken), .en(1'b1), .clk(CLK), .Q(Predict_Taken_ID));  // open: clr
  Register #(.width(4)) register_2 (.D(PC[3:0]), .en(1'b1), .clk(CLK), .Q(Predict_Address_ID));  // open: clr
  Register #(.width(1)) register_3 (.D(Entry_Found), .en(1'b1), .clk(CLK), .Q(Entry_Found_ID));  // open: clr
  Register #(.width(1)) register_4 (.D(Unkown_Entry), .en(1'b1), .clk(CLK), .Q(Unkown_Entry_ID));  // open: clr
  Register #(.width(1)) register_5 (.D(Predict_Taken_ID), .en(1'b1), .clk(CLK), .Q(Predict_Taken_EX));  // open: clr
  Register #(.width(4)) register_6 (.D(Predict_Address_ID), .en(1'b1), .clk(CLK), .Q(Predict_Address_EX));  // open: clr
  Register #(.width(1)) register_7 (.D(Entry_Found_ID), .en(1'b1), .clk(CLK), .Q(Entry_Found_EX));  // open: clr
  Register #(.width(1)) register_8 (.D(Unkown_Entry_ID), .en(1'b1), .clk(CLK), .Q(Unkown_Entry_EX));  // open: clr
  Register #(.width(1)) register_9 (.D(Predict_Taken_EX), .en(1'b1), .clk(CLK), .Q(Predict_Taken_EX_2));  // open: clr
  Register #(.width(4)) register_10 (
    .D(Predict_Address_EX), .en(1'b1), .clk(CLK), .Q(Predict_Address_EX_2));  // open: clr
  Register #(.width(1)) register_11 (.D(Entry_Found_EX), .en(1'b1), .clk(CLK), .Q(Entry_Found_EX_2));  // open: clr
  Register #(.width(1)) register_12 (.D(Unkown_Entry_EX), .en(1'b1), .clk(CLK), .Q(Unkown_Entry_EX_2));  // open: clr

  // Other names for the same wires on the sheet: Predict_Address[3:0] = PC[3:0]
endmodule

module two_bit_couter (
  input  [1:0] Input,
  input  Count_Up_Down,
  output [1:0] Output
);

  wire and_1_out, and_2_out, and_3_out, and_4_out, and_5_out, and_6_out;

  and and_1 (and_1_out, Input[1], Input[0]);
  and and_2 (and_2_out, Input[0], Count_Up_Down);
  and and_3 (and_3_out, Input[1], Count_Up_Down);
  and and_4 (and_4_out, Input[1], ~Input[0]);  // AND_Gate
  and and_5 (and_5_out, ~Input[0], Count_Up_Down);  // AND_Gate
  and and_6 (and_6_out, Input[1], Count_Up_Down);
  or or_1 (Output[1], and_1_out, and_2_out, and_3_out);
  or or_2 (Output[0], and_4_out, and_5_out, and_6_out);
endmodule
