// Logisim project Computer Architecture Project (With Pins).circ as structural Verilog: 14 circuits, main circuit main
module main (
);

  CPU cpu_1 ();  // open: out_2, out_3, out_4, out_5, out_6, out_10, out_14, out_18, out_22, out_26, out_30, out_7, out_11, out_15, out_19, out_23, out_27, out_31, out_8, out_12, out_16, out_20, out_24, out_28, out_32, out_9, out_13, out_17, out_21, out_25, out_29, out_33, out_1
endmodule

module CPU (
  output [19:0] out_1,
  output [31:0] out_2,
  output [31:0] out_3,
  output [31:0] out_4,
  output [31:0] out_5,
  output [31:0] out_6,
  output [31:0] out_7,
  output [31:0] out_8,
  output [31:0] out_9,
  output [31:0] out_10,
  output [31:0] out_11,
  output [31:0] out_12,
  output [31:0] out_13,
  output [31:0] out_14,
  output [31:0] out_15,
  output [31:0] out_16,
  output [31:0] out_17,
  output [31:0] out_18,
  output [31:0] out_19,
  output [31:0] out_20,
  output [31:0] out_21,
  output [31:0] out_22,
  output [31:0] out_23,
  output [31:0] out_24,
  output [31:0] out_25,
  output [31:0] out_26,
  output [31:0] out_27,
  output [31:0] out_28,
  output [31:0] out_29,
  output [31:0] out_30,
  output [31:0] out_31,
  output [31:0] out_32,
  output [31:0] out_33
);

  wire alu_1_condition_flag, ALUSrc, BEQ_BLT_BLTU, BNE_BGE_BGEU, CLK, ExtOp, JALR, Mem_to_Reg, MemRd, MemWr,
       RegWr, SB_Type, SSET;
  wire [1:0] RdSrc;
  wire [4:0] ALUOp, instruction_spliter_1_rd_imml5, instruction_spliter_1_s1, instruction_spliter_1_s2,
       multiplexer_2_out;
  wire [5:0] OP;
  wire [10:0] Funct;
  wire [15:0] Imm16, instruction_spliter_1_immu_imml, multiplexer_1_out;
  wire [19:0] next_pc_1_next_pc;
  wire [31:0] alu_1_result, data_memory_1_data_out, E_Imm16, instruction_memory_1_instruction,
       multiplexer_3_out, multiplexer_4_out, Output, PC_plus_1, register_file_1_read_data1,
       register_file_1_read_data2;

  Clock clock_1 (.out(CLK));
  PC pc_1 (.NextPC(next_pc_1_next_pc), .CLK(CLK), .PC(out_1));
  Instruction_Memory instruction_memory_1 (.Address(out_1), .Instruction(instruction_memory_1_instruction));
  Instruction_Spliter instruction_spliter_1 (
    .in_1(instruction_memory_1_instruction), .Op(OP), .S1(instruction_spliter_1_s1), .Immediate16(Imm16),
    .F11_ImmU11(Funct), .Rd_ImmL5(instruction_spliter_1_rd_imml5),
    .ImmU_ImmL(instruction_spliter_1_immu_imml), .S2(instruction_spliter_1_s2));
  Control_Unit control_unit_1 (
    .OP(OP), .ALUOp(ALUOp), .RdSrc(RdSrc), .RegWr(RegWr), .ExtOp(ExtOp), .ALUSrc(ALUSrc), .MemRd(MemRd),
    .MemWr(MemWr), .Mem_to_reg(Mem_to_Reg), .SB_type(SB_Type), .SSET(SSET), .JALR(JALR),
    .BNE_BGE_BGEU(BNE_BGE_BGEU), .BEQ_BLT_BLTU(BEQ_BLT_BLTU), .Funct(Funct));
  Multiplexer #(.width(16), .enable("false")) multiplexer_1 (
    .in0(Imm16), .in1(instruction_spliter_1_immu_imml), .out(multiplexer_1_out), .sel(SB_Type));
  Multiplexer #(.width(5), .enable("false")) multiplexer_2 (
    .in0(instruction_spliter_1_s2), .in1(instruction_spliter_1_rd_imml5), .out(multiplexer_2_out), .sel(SSET));
  Extender extender_1 (.in_2(multiplexer_1_out), .out_3(E_Imm16), .in_1(ExtOp));
  Register_File register_file_1 (
    .Write_Data(multiplexer_3_out), .RegWrite(RegWr), .Rd(instruction_spliter_1_rd_imml5), .CLK(CLK),
    .Read_Data1(register_file_1_read_data1), .Read_Data2(register_file_1_read_data2),
    .Rs(instruction_spliter_1_s1), .Rt(multiplexer_2_out), .R00(out_2), .R01(out_6), .R02(out_10),
    .R03(out_14), .R04(out_18), .R05(out_22), .R06(out_26), .R07(out_30), .R08(out_3), .R09(out_7),
    .R10(out_11), .R11(out_15), .R12(out_19), .R13(out_23), .R18(out_12), .R19(out_16), .R20(out_20),
    .R14(out_27), .R17(out_8), .R15(out_31), .R16(out_4), .R21(out_24), .R22(out_28), .R23(out_32),
    .R24(out_5), .R25(out_9), .R26(out_13), .R27(out_17), .R28(out_21), .R29(out_25), .R30(out_29),
    .R31(out_33));
  Multiplexer #(.select(2), .width(32), .enable("false")) multiplexer_3 (
    .in0(Output), .in1({register_file_1_read_data2[15:0], Imm16}), .in2(PC_plus_1), .in3(E_Imm16),
    .out(multiplexer_3_out), .sel(RdSrc));
  Multiplexer #(.width(32), .enable("false")) multiplexer_4 (
    .in0(E_Imm16), .in1(register_file_1_read_data2), .out(multiplexer_4_out), .sel(ALUSrc));
  Next_PC next_pc_1 (
    .Next_PC(next_pc_1_next_pc), .PC(out_1), .Immediate16(multiplexer_1_out),
    .condition_flag(alu_1_condition_flag), .JALR(JALR), .BEQ_BLT_BLTU(BEQ_BLT_BLTU),
    .BNE_BGE_BGEU(BNE_BGE_BGEU), .RS1(register_file_1_read_data1), .PC_plus_1(PC_plus_1));
  ALU alu_1 (
    .Data1(register_file_1_read_data1), .Data2(multiplexer_4_out), .Result(alu_1_result), .ALUOp(ALUOp),
    .condition_flag(alu_1_condition_flag));
  Data_Memory data_memory_1 (
    .Address(alu_1_result), .Data_out(data_memory_1_data_out), .Write(MemWr), .Read(MemRd), .CLK(CLK),
    .Data_in(register_file_1_read_data2));
  Multiplexer #(.width(32), .enable("false")) multiplexer_5 (
    .in0(alu_1_result), .in1(data_memory_1_data_out), .out(Output), .sel(Mem_to_Reg));

  // Other names for the same wires on the sheet: PC[19:0] = out_1; R00[31:0] = out_2; R01[31:0] = out_6;
  //   R02[31:0] = out_10; R03[31:0] = out_14; R04[31:0] = out_18; R05[31:0] = out_22; R06[31:0] = out_26;
  //   R07[31:0] = out_30; R08[31:0] = out_3; R09[31:0] = out_7; R10[31:0] = out_11; R11[31:0] = out_15;
  //   R12[31:0] = out_19; R13[31:0] = out_23; R14[31:0] = out_27; R15[31:0] = out_31; R16[31:0] = out_4;
  //   R17[31:0] = out_8; R18[31:0] = out_12; R19[31:0] = out_16; R20[31:0] = out_20; R21[31:0] = out_24;
  //   R22[31:0] = out_28; R23[31:0] = out_32; R24[31:0] = out_5; R25[31:0] = out_9; R26[31:0] = out_13;
  //   R27[31:0] = out_17; R28[31:0] = out_21; R29[31:0] = out_25; R30[31:0] = out_29; R31[31:0] = out_33
endmodule

module Register_File (
  input  [4:0] Rs,
  input  [4:0] Rt,
  input  [4:0] Rd,
  input  CLK,
  input  [31:0] Write_Data,
  input  RegWrite,
  output [31:0] R00,
  output [31:0] R01,
  output [31:0] R02,
  output [31:0] R03,
  output [31:0] R04,
  output [31:0] R05,
  output [31:0] R06,
  output [31:0] R07,
  output [31:0] R08,
  output [31:0] R09,
  output [31:0] R10,
  output [31:0] R11,
  output [31:0] R12,
  output [31:0] Read_Data1,
  output [31:0] R13,
  output [31:0] R14,
  output [31:0] R15,
  output [31:0] R16,
  output [31:0] R17,
  output [31:0] Read_Data2,
  output [31:0] R18,
  output [31:0] R19,
  output [31:0] R20,
  output [31:0] R21,
  output [31:0] R22,
  output [31:0] R23,
  output [31:0] R24,
  output [31:0] R25,
  output [31:0] R26,
  output [31:0] R27,
  output [31:0] R28,
  output [31:0] R29,
  output [31:0] R30,
  output [31:0] R31
);

  wire demultiplexer_1_out0, demultiplexer_1_out1, demultiplexer_1_out2, demultiplexer_1_out3,
       demultiplexer_1_out4, demultiplexer_1_out5, demultiplexer_1_out6, demultiplexer_1_out7,
       demultiplexer_1_out8, demultiplexer_1_out9, demultiplexer_1_out10, demultiplexer_1_out11,
       demultiplexer_1_out12, demultiplexer_1_out13, demultiplexer_1_out14, demultiplexer_1_out15,
       demultiplexer_1_out16, demultiplexer_1_out17, demultiplexer_1_out18, demultiplexer_1_out19,
       demultiplexer_1_out20, demultiplexer_1_out21, demultiplexer_1_out22, demultiplexer_1_out23,
       demultiplexer_1_out24, demultiplexer_1_out25, demultiplexer_1_out26, demultiplexer_1_out27,
       demultiplexer_1_out28, demultiplexer_1_out29, demultiplexer_1_out30, demultiplexer_1_out31;

  Demultiplexer #(.select(5), .enable("false")) demultiplexer_1 (
    .out0(demultiplexer_1_out0), .out1(demultiplexer_1_out1), .out2(demultiplexer_1_out2),
    .out3(demultiplexer_1_out3), .out4(demultiplexer_1_out4), .out5(demultiplexer_1_out5),
    .out6(demultiplexer_1_out6), .out7(demultiplexer_1_out7), .out8(demultiplexer_1_out8),
    .out9(demultiplexer_1_out9), .out10(demultiplexer_1_out10), .out11(demultiplexer_1_out11),
    .out12(demultiplexer_1_out12), .out13(demultiplexer_1_out13), .out14(demultiplexer_1_out14),
    .out15(demultiplexer_1_out15), .out16(demultiplexer_1_out16), .out17(demultiplexer_1_out17),
    .out18(demultiplexer_1_out18), .out19(demultiplexer_1_out19), .out20(demultiplexer_1_out20),
    .out21(demultiplexer_1_out21), .out22(demultiplexer_1_out22), .out23(demultiplexer_1_out23),
    .out24(demultiplexer_1_out24), .out25(demultiplexer_1_out25), .out26(demultiplexer_1_out26),
    .out27(demultiplexer_1_out27), .out28(demultiplexer_1_out28), .out29(demultiplexer_1_out29),
    .out30(demultiplexer_1_out30), .out31(demultiplexer_1_out31), .in(RegWrite), .sel(Rd));
  Register #(.width(32)) u_R00 (.D({32{1'b0}}), .en(demultiplexer_1_out0), .clk(CLK), .Q(R00));  // open: clr
  Register #(.width(32)) u_R01 (.D(Write_Data), .en(demultiplexer_1_out1), .clk(CLK), .Q(R01));  // open: clr
  Register #(.width(32)) u_R02 (.D(Write_Data), .en(demultiplexer_1_out2), .clk(CLK), .Q(R02));  // open: clr
  Register #(.width(32)) u_R03 (.D(Write_Data), .en(demultiplexer_1_out3), .clk(CLK), .Q(R03));  // open: clr
  Register #(.width(32)) u_R04 (.D(Write_Data), .en(demultiplexer_1_out4), .clk(CLK), .Q(R04));  // open: clr
  Register #(.width(32)) u_R05 (.D(Write_Data), .en(demultiplexer_1_out5), .clk(CLK), .Q(R05));  // open: clr
  Register #(.width(32)) u_R06 (.D(Write_Data), .en(demultiplexer_1_out6), .clk(CLK), .Q(R06));  // open: clr
  Register #(.width(32)) u_R07 (.D(Write_Data), .en(demultiplexer_1_out7), .clk(CLK), .Q(R07));  // open: clr
  Register #(.width(32)) u_R08 (.D(Write_Data), .en(demultiplexer_1_out8), .clk(CLK), .Q(R08));  // open: clr
  Register #(.width(32)) u_R09 (.D(Write_Data), .en(demultiplexer_1_out9), .clk(CLK), .Q(R09));  // open: clr
  Register #(.width(32)) u_R10 (.D(Write_Data), .en(demultiplexer_1_out10), .clk(CLK), .Q(R10));  // open: clr
  Register #(.width(32)) u_R11 (.D(Write_Data), .en(demultiplexer_1_out11), .clk(CLK), .Q(R11));  // open: clr
  Register #(.width(32)) u_R12 (.D(Write_Data), .en(demultiplexer_1_out12), .clk(CLK), .Q(R12));  // open: clr
  Register #(.width(32)) u_R13 (.D(Write_Data), .en(demultiplexer_1_out13), .clk(CLK), .Q(R13));  // open: clr
  Register #(.width(32)) u_R14 (.D(Write_Data), .en(demultiplexer_1_out14), .clk(CLK), .Q(R14));  // open: clr
  Register #(.width(32)) u_R15 (.D(Write_Data), .en(demultiplexer_1_out15), .clk(CLK), .Q(R15));  // open: clr
  Register #(.width(32)) u_R16 (.D(Write_Data), .en(demultiplexer_1_out16), .clk(CLK), .Q(R16));  // open: clr
  Register #(.width(32)) u_R17 (.D(Write_Data), .en(demultiplexer_1_out17), .clk(CLK), .Q(R17));  // open: clr
  Register #(.width(32)) u_R18 (.D(Write_Data), .en(demultiplexer_1_out18), .clk(CLK), .Q(R18));  // open: clr
  Register #(.width(32)) u_R19 (.D(Write_Data), .en(demultiplexer_1_out19), .clk(CLK), .Q(R19));  // open: clr
  Register #(.width(32)) u_R20 (.D(Write_Data), .en(demultiplexer_1_out20), .clk(CLK), .Q(R20));  // open: clr
  Register #(.width(32)) u_R21 (.D(Write_Data), .en(demultiplexer_1_out21), .clk(CLK), .Q(R21));  // open: clr
  Register #(.width(32)) u_R22 (.D(Write_Data), .en(demultiplexer_1_out22), .clk(CLK), .Q(R22));  // open: clr
  Register #(.width(32)) u_R23 (.D(Write_Data), .en(demultiplexer_1_out23), .clk(CLK), .Q(R23));  // open: clr
  Register #(.width(32)) u_R24 (.D(Write_Data), .en(demultiplexer_1_out24), .clk(CLK), .Q(R24));  // open: clr
  Register #(.width(32)) u_R25 (.D(Write_Data), .en(demultiplexer_1_out25), .clk(CLK), .Q(R25));  // open: clr
  Register #(.width(32)) u_R26 (.D(Write_Data), .en(demultiplexer_1_out26), .clk(CLK), .Q(R26));  // open: clr
  Register #(.width(32)) u_R27 (.D(Write_Data), .en(demultiplexer_1_out27), .clk(CLK), .Q(R27));  // open: clr
  Register #(.width(32)) u_R28 (.D(Write_Data), .en(demultiplexer_1_out28), .clk(CLK), .Q(R28));  // open: clr
  Register #(.width(32)) u_R29 (.D(Write_Data), .en(demultiplexer_1_out29), .clk(CLK), .Q(R29));  // open: clr
  Register #(.width(32)) u_R30 (.D(Write_Data), .en(demultiplexer_1_out30), .clk(CLK), .Q(R30));  // open: clr
  Register #(.width(32)) u_R31 (.D(Write_Data), .en(demultiplexer_1_out31), .clk(CLK), .Q(R31));  // open: clr
  Multiplexer #(.select(5), .width(32), .enable("false")) multiplexer_1 (
    .in0(R00), .in1(R01), .in2(R02), .in3(R03), .in4(R04), .in5(R05), .in6(R06), .in7(R07), .in8(R08),
    .in9(R09), .in10(R10), .in11(R11), .in12(R12), .in13(R13), .in14(R14), .in15(R15), .in16(R16),
    .in17(R17), .in18(R18), .in19(R19), .in20(R20), .in21(R21), .in22(R22), .in23(R23), .in24(R24),
    .in25(R25), .in26(R26), .in27(R27), .in28(R28), .in29(R29), .in30(R30), .in31(R31), .out(Read_Data1),
    .sel(Rs));
  Multiplexer #(.select(5), .width(32), .enable("false")) multiplexer_2 (
    .in0(R00), .in1(R01), .in2(R02), .in3(R03), .in4(R04), .in5(R05), .in6(R06), .in7(R07), .in8(R08),
    .in9(R09), .in10(R10), .in11(R11), .in12(R12), .in13(R13), .in14(R14), .in15(R15), .in16(R16),
    .in17(R17), .in18(R18), .in19(R19), .in20(R20), .in21(R21), .in22(R22), .in23(R23), .in24(R24),
    .in25(R25), .in26(R26), .in27(R27), .in28(R28), .in29(R29), .in30(R30), .in31(R31), .out(Read_Data2),
    .sel(Rt));
endmodule

module ALU (
  input  [4:0] ALUOp,
  input  [31:0] Data1,
  input  [31:0] Data2,
  output condition_flag,
  output [31:0] Result
);

  wire adder_1_carry_flag, adder_1_overflow_flag, not_1_out, xor_2_out, zero_detector_1_out_2;
  wire [30:0] multiplier_1_out;
  wire [31:0] and_1_out, Arithmetic, Logical, MUL, not_2_out, or_1_out, SEQ, Shift, SLT, SLTU, xor_1_out;

  Adder adder_1 (
    .Data1(Data1), .Data2(Data2), .Data_out(Arithmetic), .carry_flag(adder_1_carry_flag),
    .overflow_flag(adder_1_overflow_flag), .Add_Sub(ALUOp[0]));
  assign and_1_out = Data1 & Data2;  // AND_Gate and_1, 32 bits wide
  assign or_1_out = Data1 | Data2;  // OR_Gate or_1, 32 bits wide
  assign xor_1_out = Data1 ^ Data2;  // XOR_Gate xor_1, 32 bits wide
  Multiplier #(.width(31)) multiplier_1 (.a(Data1[30:0]), .b(Data2[30:0]), .out(multiplier_1_out));  // open: cin, cout
  not not_1 (not_1_out, adder_1_carry_flag);
  Zero_Detector zero_detector_1 (.in_1(Arithmetic), .out_2(zero_detector_1_out_2));
  assign not_2_out = ~or_1_out;  // NOT_Gate not_2, 32 bits wide
  Shifter shifter_1 (.Shift_Amount(Data2[4:0]), .Data_in(Data1), .Shift_Rotate(ALUOp[1:0]), .Data_out(Shift));
  assign SLT = {{31{1'b0}}, xor_2_out};  // Bit_Extender bit_extender_1
  xor xor_2 (xor_2_out, adder_1_overflow_flag, Arithmetic[31]);
  assign SLTU = {{31{1'b0}}, not_1_out};  // Bit_Extender bit_extender_2
  assign SEQ = {{31{1'b0}}, zero_detector_1_out_2};  // Bit_Extender bit_extender_3
  Multiplexer #(.select(2), .width(32), .enable("false")) multiplexer_1 (
    .in0(and_1_out), .in1(or_1_out), .in2(not_2_out), .in3(xor_1_out), .out(Logical), .sel(ALUOp[1:0]));
  assign MUL = {{1{multiplier_1_out[30]}}, multiplier_1_out};  // Bit_Extender bit_extender_4
  Multiplexer #(.select(3), .width(32), .enable("false")) multiplexer_2 (
    .in0(Shift), .in1(Arithmetic), .in2(SLT), .in3(SLTU), .in4(SEQ), .in5(Logical), .in6(MUL),
    .out({Result[31:1], condition_flag}), .sel(ALUOp[4:2]));  // open: in7

  assign Result[0] = condition_flag;

  // Other names for the same wires on the sheet: ALU_Selection[2:0] = ALUOp[4:2]
endmodule

module PC (
  input  [19:0] NextPC,
  input  CLK,
  output [19:0] PC
);

  Register #(.width(20)) u_PC (.D(NextPC), .en(1'b1), .clk(CLK), .Q(PC));  // open: clr
endmodule

module Instruction_Memory (
  input  [19:0] Address,
  output [31:0] Instruction
);

  ROM #(.addrWidth(20), .dataWidth(32)) rom_1 (.addr(Address), .data(Instruction));

  // Notes on the sheet:
  //   contents of rom_1 (hex, n*v repeats v):
  //   384004d 1234020d 5678020e 140945 12508c0 834100 50 10090 200d0 a42100 841100 c31180 30d2 820880
  //   ffe00712 40011 1a31280 245380 4453c0 57684 1a01cf 4545024d 4545028d 95095 ffff0dcb 12 1431140 50
  //   50890 608d0 1631100 40011 380f
endmodule

module Data_Memory (
  input  Read,
  input  Write,
  input  [31:0] Address,
  input  CLK,
  input  [31:0] Data_in,
  output [31:0] Data_out
);

  RAM #(.addrWidth(20), .dataWidth(32), .trigger("falling"), .databus("bibus")) ram_1 (
    .addr(Address[19:0]), .we(Write), .oe(Read), .clk(CLK), .din(Data_in), .dout(Data_out));
endmodule

module Instruction_Spliter (
  input  [31:0] in_1,
  output [15:0] Immediate16,
  output [10:0] F11_ImmU11,
  output [4:0] S2,
  output [4:0] Rd_ImmL5,
  output [5:0] Op,
  output [4:0] S1,
  output [15:0] ImmU_ImmL
);


  assign F11_ImmU11 = in_1[31:21];
  assign Immediate16 = in_1[31:16];
  assign ImmU_ImmL = {in_1[31:21], in_1[10:6]};
  assign Op = in_1[5:0];
  assign Rd_ImmL5 = in_1[10:6];
  assign S1 = in_1[15:11];
  assign S2 = in_1[20:16];
endmodule

module Next_PC (
  input  JALR,
  input  [31:0] RS1,
  input  [15:0] Immediate16,
  input  BNE_BGE_BGEU,
  input  BEQ_BLT_BLTU,
  input  [19:0] PC,
  input  condition_flag,
  output [19:0] Next_PC,
  output [31:0] PC_plus_1
);

  wire and_1_out, and_2_out;
  wire [0:0] or_1_out;
  wire [19:0] adder_1_out, adder_2_out, adder_3_out, bit_extender_1_out;

  assign bit_extender_1_out = {{4{Immediate16[15]}}, Immediate16};  // Bit_Extender bit_extender_1
  Adder_part #(.width(20)) adder_1 (.a(20'h1), .b(PC), .out(adder_1_out));  // open: cin, cout
  Multiplexer #(.select(2), .width(20), .enable("false")) multiplexer_1 (
    .in0(adder_1_out), .in1(adder_3_out), .in2(adder_2_out), .out(Next_PC), .sel({JALR, or_1_out[0]}));  // open: in3
  Adder_part #(.width(20)) adder_2 (.a(RS1[19:0]), .b(bit_extender_1_out), .out(adder_2_out));  // open: cin, cout
  Adder_part #(.width(20)) adder_3 (.a(bit_extender_1_out), .b(PC), .out(adder_3_out));  // open: cin, cout
  assign PC_plus_1 = {{12{1'b0}}, adder_1_out};  // Bit_Extender bit_extender_2
  or or_1 (or_1_out[0], and_1_out, and_2_out);
  and and_1 (and_1_out, BEQ_BLT_BLTU, condition_flag);
  and and_2 (and_2_out, BNE_BGE_BGEU, ~condition_flag);  // AND_Gate
endmodule

module Zero_Detector (
  input  [31:0] in_1,
  output out_2
);

  nor nor_1 (out_2, in_1[31], in_1[30], in_1[29], in_1[28], in_1[27], in_1[26], in_1[25], in_1[24], in_1[23], in_1[22], in_1[21], in_1[20], in_1[19], in_1[18], in_1[17], in_1[16], in_1[15], in_1[14], in_1[13], in_1[12], in_1[11], in_1[10], in_1[9], in_1[8], in_1[7], in_1[6], in_1[5], in_1[4], in_1[3], in_1[2], in_1[1], in_1[0]);
endmodule

module Shifter (
  input  [4:0] Shift_Amount,
  input  [31:0] Data_in,
  input  [1:0] Shift_Rotate,
  output [31:0] Data_out
);

  wire [31:0] shifter_1_out, shifter_2_out, shifter_3_out, shifter_4_out;

  Shifter_part #(.width(32)) shifter_1 (.in(Data_in), .\dist (Shift_Amount), .out(shifter_1_out));
  Shifter_part #(.width(32), .shift("lr")) shifter_2 (.in(Data_in), .\dist (Shift_Amount), .out(shifter_2_out));
  Shifter_part #(.width(32), .shift("ar")) shifter_3 (.in(Data_in), .\dist (Shift_Amount), .out(shifter_3_out));
  Shifter_part #(.width(32), .shift("rr")) shifter_4 (.in(Data_in), .\dist (Shift_Amount), .out(shifter_4_out));
  Multiplexer #(.select(2), .width(32), .enable("false")) multiplexer_1 (
    .in0(shifter_1_out), .in1(shifter_2_out), .in2(shifter_3_out), .in3(shifter_4_out), .out(Data_out),
    .sel(Shift_Rotate));

  // Notes on the sheet:
  //   Operation
endmodule

module Adder (
  input  Add_Sub,
  input  [31:0] Data1,
  input  [31:0] Data2,
  output [31:0] Data_out,
  output carry_flag,
  output overflow_flag
);

  wire xor_2_out, xor_3_out;
  wire [31:0] bit_extender_1_out, xor_1_out;

  assign bit_extender_1_out = {{31{Add_Sub}}, Add_Sub};  // Bit_Extender bit_extender_1
  assign xor_1_out = Data2 ^ bit_extender_1_out;  // XOR_Gate xor_1, 32 bits wide
  Adder_part #(.width(32)) adder_1 (.a(Data1), .b(xor_1_out), .out(Data_out), .cin(Add_Sub), .cout(carry_flag));
  xor xor_2 (xor_2_out, Data_out[31], Data1[31]);
  xor xor_3 (xor_3_out, Data_out[31], xor_1_out[31]);
  and and_1 (overflow_flag, xor_2_out, xor_3_out);
endmodule

module Control_Unit (
  input  [5:0] OP,
  input  [10:0] Funct,
  output [4:0] ALUOp,
  output [1:0] RdSrc,
  output RegWr,
  output ExtOp,
  output ALUSrc,
  output MemRd,
  output MemWr,
  output Mem_to_reg,
  output SB_type,
  output SSET,
  output JALR,
  output BNE_BGE_BGEU,
  output BEQ_BLT_BLTU
);

  ROM #(.addrWidth(9), .dataWidth(18)) rom_1 (
    .addr({OP[4:0], Funct[3:0]}),
    .data({ALUOp, RdSrc, RegWr, ExtOp, ALUSrc, MemRd, MemWr, Mem_to_reg, SB_type, SSET, JALR, BNE_BGE_BGEU, BEQ_BLT_BLTU}));

  // Notes on the sheet:
  //   contents of rom_1 (hex, n*v repeats v):
  //   500 2500 4500 6500 8500 a500 12500 1a500 22500 2e500 2a500 28500 2c500 30500 0 0 16*400 16*2400
  //   16*4400 16*6400 16*8600 16*12600 16*1a400 16*22600 16*2e400 16*2a400 16*28400 16*2c400 16*1e00
  //   16*c08 16*1404 16*86a0 16*8250 16*22111 16*22112 16*12111 16*12112 16*1a111 16*1a112
endmodule

module Extender (
  input  in_1,
  input  [15:0] in_2,
  output [31:0] out_3
);

  wire [31:0] bit_extender_1_out, bit_extender_2_out;

  assign bit_extender_1_out = {{16{1'b0}}, in_2};  // Bit_Extender bit_extender_1
  assign bit_extender_2_out = {{16{in_2[15]}}, in_2};  // Bit_Extender bit_extender_2
  Multiplexer #(.width(32), .enable("false")) multiplexer_1 (
    .in0(bit_extender_1_out), .in1(bit_extender_2_out), .out(out_3), .sel(in_1));
endmodule
